# Fritzing sketch hbrucke (saved by Fritzing 0.9.3b)
breadboards: 1

parts:
  Raspberry_Pi1 = Raspberry Pi B rev2
  Q1 = PNP-Transistor [package="TO92 [THT]"]
  Q2 = PNP-Transistor [package="TO92 [THT]"]
  Q3 = NPN-Transistor [package="TO92 [THT]"]
  Q4 = NPN-Transistor [package="TO92 [THT]"]
  R2 = Resistor [tolerance=±5% resistance=2.2k package=THT]
  R3 = Resistor [tolerance=±5% resistance=2.2k package=THT]
  R4 = Resistor [tolerance=±5% resistance=2.2k package=THT]
  R5 = Resistor [tolerance=±5% resistance=2.2k package=THT]
  M1 = DC Motor

nets:
  N1: Raspberry_Pi1.GPIO_17, R3.Pin_0, R5.Pin_0
  N2: Raspberry_Pi1.GPIO_4, R2.Pin_0, R4.Pin_0
  N3: Q1.E, Q3.E, M1.pin_2
  N4: Q1.B, R3.Pin_1
  N5: Q1.C, Q2.C
  N6: Q2.E, Q4.E, M1.pin_1
  N7: Q2.B, R4.Pin_1
  N8: Q3.B, R5.Pin_1
  N9: Q3.C, Q4.C
  N10: Q4.B, R2.Pin_1
