# Fritzing sketch led (saved by Fritzing 0.9.3b)
breadboards: 1

parts:
  Raspberry_Pi1 = Raspberry Pi B rev2
  LED1 = LED - 5mm [color="Red (633nm)" package="5 mm [THT]"]
  R1 = Resistor [tolerance=±5% resistance=220 package="2010 [SMD]"]
  S1 = Momentary Switch [package=ksa_sealed_tac_switch]

nets:
  N1: Raspberry_Pi1.GPIO_2, S1.3, S1.4
  N2: Raspberry_Pi1.GND, LED1.cathode, S1.1, S1.2
  N3: Raspberry_Pi1.GPIO_7, R1.Pin_1
  N4: LED1.anode, R1.Pin_0
