# Fritzing sketch ultraschall (saved by Fritzing 0.9.3b)
breadboards: 1

parts:
  Raspberry_Pi1 = Raspberry Pi B rev2
  hc-sr1 = hc-sr04
  R1 = Resistor [tolerance=±5% resistance=220 package=THT]
  R2 = Resistor [tolerance=±5% resistance=220 package=THT]
  R3 = Resistor [tolerance=±5% resistance=220 package=THT]
  LED1 = LED - 5mm [color="Red (633nm)" package="5 mm [THT]"]

nets:
  5V: Raspberry_Pi1.5V, hc-sr1.VCC
  GND: Raspberry_Pi1.GND, hc-sr1.GND, R2.Pin_0, R3.Pin_1
  N1: Raspberry_Pi1.GPIO_18, hc-sr1.Trig
  N2: Raspberry_Pi1.GPIO_24, R1.Pin_1, R2.Pin_1
  N3: Raspberry_Pi1.GPIO_25, LED1.anode
  N4: hc-sr1.Echo, R1.Pin_0
  N5: R3.Pin_0, LED1.cathode
