# Fritzing sketch servo (saved by Fritzing 0.9.3b)
breadboards: 1

parts:
  Raspberry_Pi1 = Raspberry Pi B rev2
  J1 = Basic Servo

nets:
  3V3: Raspberry_Pi1.3V3, J1.vcc
  GND: Raspberry_Pi1.GND, J1.gnd
  N1: Raspberry_Pi1.GPIO_14, J1.pulse
